// Logisim project ETFStudent.circ as structural Verilog: 8 circuits, main circuit REG32_LD
module REG32_LD (
  input  [31:0] I15__0,
  input  LD,
  input  mr,
  input  CLK,
  output [31:0] A15__0
);

  // REG16_LD reg16_ld_1: pin names not known; wires that end beside it: CLK, mr, I15__0[31:16], A15__0[31:16], LD
  // REG16_LD reg16_ld_2: pin names not known; wires that end beside it: CLK, mr, I15__0[15:0], A15__0[15:0], LD

  // Notes on the sheet:
  //   __
endmodule

module KMADR (
  input  immed,
  input  memdir,
  input  regdir,
  input  regindpom,
  output [3:0] Adr3__0
);

  assign Adr3__0 = immed ? 4'b0010 : 4'bz;  // Controlled_Buffer controlled_buffer_1
  assign Adr3__0 = memdir ? 4'b0100 : 4'bz;  // Controlled_Buffer controlled_buffer_2
  assign Adr3__0 = regdir ? 4'b0101 : 4'bz;  // Controlled_Buffer controlled_buffer_3
  assign Adr3__0 = regindpom ? 4'b0111 : 4'bz;  // Controlled_Buffer controlled_buffer_4
endmodule

module KMOPR (
  input  LD,
  input  ST,
  input  ADD,
  input  SUB,
  input  BLSS,
  input  JLEQ,
  input  JMP,
  input  JSR,
  input  RTS,
  input  RTI,
  input  HALT,
  output [5:0] Adr5__0
);

  assign Adr5__0 = LD ? 6'b000010 : 6'bz;  // Controlled_Buffer controlled_buffer_1
  assign Adr5__0 = ST ? 6'b000100 : 6'bz;  // Controlled_Buffer controlled_buffer_2
  assign Adr5__0 = ADD ? 6'b001010 : 6'bz;  // Controlled_Buffer controlled_buffer_3
  assign Adr5__0 = SUB ? 6'b001100 : 6'bz;  // Controlled_Buffer controlled_buffer_4
  assign Adr5__0 = BLSS ? 6'b001110 : 6'bz;  // Controlled_Buffer controlled_buffer_5
  assign Adr5__0 = JLEQ ? 6'b010000 : 6'bz;  // Controlled_Buffer controlled_buffer_6
  assign Adr5__0 = JMP ? 6'b010001 : 6'bz;  // Controlled_Buffer controlled_buffer_7
  assign Adr5__0 = JSR ? 6'b010010 : 6'bz;  // Controlled_Buffer controlled_buffer_8
  assign Adr5__0 = RTS ? 6'b010111 : 6'bz;  // Controlled_Buffer controlled_buffer_9
  assign Adr5__0 = RTI ? 6'b011110 : 6'bz;  // Controlled_Buffer controlled_buffer_10
  assign Adr5__0 = HALT ? 6'b100010 : 6'bz;  // Controlled_Buffer controlled_buffer_11
endmodule

module REG6_INC_LD (
  input  [5:0] I5__0,
  input  LD,
  input  INC,
  input  mr,
  input  CLK,
  output [5:0] A5__0
);

  wire reg2m_inc_ld_1_p7, reg2m_inc_ld_2_p8;

  // REG2m_INC_LD reg2m_inc_ld_1: pin names not known; wires that end beside it: CLK, mr, I5__0[5:4], A5__0[5:4], LD, INC, reg2m_inc_ld_1_p7
  // REG2m_INC_LD reg2m_inc_ld_2: pin names not known; wires that end beside it: CLK, reg2m_inc_ld_1_p7, mr, I5__0[3:2], A5__0[3:2], LD, INC, reg2m_inc_ld_2_p8
  // REG2m_INC_LD reg2m_inc_ld_3: pin names not known; wires that end beside it: CLK, reg2m_inc_ld_2_p8, mr, I5__0[1:0], A5__0[1:0], LD, INC, INC

  // Notes on the sheet:
  //   __
endmodule

module ROM32x24 (
  input  [4:0] A4__0,
  input  CS,
  output [23:0] DOUT
);

  ROM #(.addrWidth(5), .dataWidth(24)) rom_1 (.addr(A4__0), .data(DOUT), .sel(CS));
endmodule

module GPR16x16 (
  input  [15:0] DI15__0,
  input  [3:0] A3__0,
  input  WR,
  input  CLK,
  input  [7:0] REGSIG7__0,
  output [15:0] DO15__0
);

  wire and_1_out, and_2_out, and_7_out, and_8_out, and_9_out, and_10_out, and_12_out, and_14_out, and_15_out,
       and_16_out, CS0, CS1, CS2, CS3, CS4, CS5, CS6, CS7, CS8, CS9, CS10, CS11, CS12, CS13, CS14, CS15,
       mp4_16b_1_p5, mp4_16b_3_p5, reg16_1_p4, reg16_inc_ld_1_p2, reg16_inc_ld_1_p4, reg16_inc_ld_2_p4,
       reg16_ld_2_p4, reg16_ld_3_p4, reg16_ld_4_p4, reg16_ld_5_p4, reg16_ld_9_p4, reg16_ld_11_p4;
  wire [15:0] reg16_1_p3, reg16_inc_ld_1_p3, reg16_inc_ld_2_p3, reg16_ld_1_p3, reg16_ld_2_p3, reg16_ld_3_p3,
       reg16_ld_4_p3, reg16_ld_5_p3, reg16_ld_6_p3, reg16_ld_7_p3, reg16_ld_8_p3, reg16_ld_9_p3,
       reg16_ld_10_p3, reg16_ld_11_p3, reg16_ld_12_p3, reg16_ld_13_p3;

  // DC4_16 dc4_16_1: pin names not known; wires that end beside it: A3__0, 1'b1, CS0, CS1, CS2, CS3, CS4, CS5, CS6, CS7, CS8, CS9, CS10, CS11, CS12, CS13, CS14, CS15
  // MP4_16b mp4_16b_1: pin names not known; wires that end beside it: 1'b0, REGSIG7__0[5], 16'hf000, DI15__0, mp4_16b_1_p5, 1'b1
  // REG16 reg16_1: pin names not known; wires that end beside it: CLK, mp4_16b_1_p5, reg16_1_p3, reg16_1_p4, REGSIG7__0[3], REGSIG7__0[4]
  assign DO15__0 = CS1 ? reg16_1_p3 : 16'bz;  // Controlled_Buffer controlled_buffer_1
  or or_1 (reg16_1_p4, and_2_out, REGSIG7__0[0]);
  and and_1 (and_1_out, CS3, WR);
  // REG16_LD reg16_ld_1: pin names not known; wires that end beside it: CLK, DI15__0, reg16_ld_1_p3, and_1_out
  assign DO15__0 = CS3 ? reg16_ld_1_p3 : 16'bz;  // Controlled_Buffer controlled_buffer_2
  and and_2 (and_2_out, CS1, WR);
  // REG16_INC_LD reg16_inc_ld_1: pin names not known; wires that end beside it: CLK, reg16_inc_ld_1_p2, reg16_inc_ld_1_p3, reg16_inc_ld_1_p4, REGSIG7__0[1]
  assign DO15__0 = CS2 ? reg16_inc_ld_1_p3 : 16'bz;  // Controlled_Buffer controlled_buffer_3
  // MP4_16b mp4_16b_2: pin names not known; wires that end beside it: 1'b0, REGSIG7__0[2], 16'h1000, DI15__0, reg16_inc_ld_1_p2, 1'b1
  // REG16_LD reg16_ld_2: pin names not known; wires that end beside it: CLK, DI15__0, reg16_ld_2_p3, reg16_ld_2_p4
  assign DO15__0 = CS4 ? reg16_ld_2_p3 : 16'bz;  // Controlled_Buffer controlled_buffer_4
  // REG16_LD reg16_ld_3: pin names not known; wires that end beside it: CLK, DI15__0, reg16_ld_3_p3, reg16_ld_3_p4
  assign DO15__0 = CS5 ? reg16_ld_3_p3 : 16'bz;  // Controlled_Buffer controlled_buffer_5
  // REG16_LD reg16_ld_4: pin names not known; wires that end beside it: CLK, DI15__0, reg16_ld_4_p3, reg16_ld_4_p4
  assign DO15__0 = CS6 ? reg16_ld_4_p3 : 16'bz;  // Controlled_Buffer controlled_buffer_6
  // REG16_LD reg16_ld_5: pin names not known; wires that end beside it: CLK, DI15__0, reg16_ld_5_p3, reg16_ld_5_p4
  assign DO15__0 = CS7 ? reg16_ld_5_p3 : 16'bz;  // Controlled_Buffer controlled_buffer_7
  or or_2 (reg16_inc_ld_1_p4, and_7_out, REGSIG7__0[0]);
  and and_3 (reg16_ld_2_p4, CS4, WR);
  and and_4 (reg16_ld_3_p4, CS5, WR);
  and and_5 (reg16_ld_4_p4, CS6, WR);
  and and_6 (reg16_ld_5_p4, CS7, WR);
  and and_7 (and_7_out, CS2, WR);
  and and_8 (and_8_out, CS8, WR);
  // REG16_LD reg16_ld_6: pin names not known; wires that end beside it: CLK, DI15__0, reg16_ld_6_p3, and_8_out
  assign DO15__0 = CS8 ? reg16_ld_6_p3 : 16'bz;  // Controlled_Buffer controlled_buffer_8
  and and_9 (and_9_out, CS9, WR);
  // REG16_LD reg16_ld_7: pin names not known; wires that end beside it: CLK, DI15__0, reg16_ld_7_p3, and_9_out
  assign DO15__0 = CS9 ? reg16_ld_7_p3 : 16'bz;  // Controlled_Buffer controlled_buffer_9
  and and_10 (and_10_out, CS10, WR);
  // REG16_LD reg16_ld_8: pin names not known; wires that end beside it: CLK, DI15__0, reg16_ld_8_p3, and_10_out
  assign DO15__0 = CS10 ? reg16_ld_8_p3 : 16'bz;  // Controlled_Buffer controlled_buffer_10
  // REG16_LD reg16_ld_9: pin names not known; wires that end beside it: CLK, DI15__0, reg16_ld_9_p3, reg16_ld_9_p4
  and and_11 (reg16_ld_9_p4, CS11, WR);
  assign DO15__0 = CS11 ? reg16_ld_9_p3 : 16'bz;  // Controlled_Buffer controlled_buffer_11
  // MP4_16b mp4_16b_3: pin names not known; wires that end beside it: 1'b0, REGSIG7__0[6], {16{1'b0}}, DI15__0, mp4_16b_3_p5, 1'b1
  // REG16_INC_LD reg16_inc_ld_2: pin names not known; wires that end beside it: CLK, mp4_16b_3_p5, reg16_inc_ld_2_p3, reg16_inc_ld_2_p4
  assign DO15__0 = CS0 ? reg16_inc_ld_2_p3 : 16'bz;  // Controlled_Buffer controlled_buffer_12
  or or_3 (reg16_inc_ld_2_p4, and_16_out, REGSIG7__0[0]);
  and and_12 (and_12_out, CS12, WR);
  // REG16_LD reg16_ld_10: pin names not known; wires that end beside it: CLK, DI15__0, reg16_ld_10_p3, and_12_out
  assign DO15__0 = CS12 ? reg16_ld_10_p3 : 16'bz;  // Controlled_Buffer controlled_buffer_13
  // REG16_LD reg16_ld_11: pin names not known; wires that end beside it: CLK, DI15__0, reg16_ld_11_p3, reg16_ld_11_p4
  and and_13 (reg16_ld_11_p4, CS13, WR);
  assign DO15__0 = CS13 ? reg16_ld_11_p3 : 16'bz;  // Controlled_Buffer controlled_buffer_14
  and and_14 (and_14_out, CS14, WR);
  // REG16_LD reg16_ld_12: pin names not known; wires that end beside it: CLK, DI15__0, reg16_ld_12_p3, and_14_out
  assign DO15__0 = CS14 ? reg16_ld_12_p3 : 16'bz;  // Controlled_Buffer controlled_buffer_15
  and and_15 (and_15_out, CS15, WR);
  // REG16_LD reg16_ld_13: pin names not known; wires that end beside it: CLK, DI15__0, reg16_ld_13_p3, and_15_out
  assign DO15__0 = CS15 ? reg16_ld_13_p3 : 16'bz;  // Controlled_Buffer controlled_buffer_16
  and and_16 (and_16_out, CS0, WR);

  // Other names for the same wires on the sheet: inREG[15:0] = DI15__0; outREG[15:0] = DO15__0; rst = REGSIG7__0[0];
  //   incPC = REGSIG7__0[1]; mxPC0 = REGSIG7__0[2]; incSP = REGSIG7__0[3]; decSP = REGSIG7__0[4];
  //   mxSP0 = REGSIG7__0[5]; mxACC0 = REGSIG7__0[6]

  // Notes on the sheet:
  //   SP registar
  //   PC registar
  //   ACC registar
endmodule

module ROM32x32 (
  input  [4:0] A4__0,
  input  CS,
  output [31:0] DOUT
);

  ROM #(.addrWidth(5), .dataWidth(32)) rom_1 (.addr(A4__0), .data(DOUT), .sel(CS));
endmodule

module KMADR6 (
  input  immed,
  input  memdir,
  input  regdir,
  input  memind,
  input  postincr,
  input  pcrelpom,
  output [4:0] Adr3__0
);

  assign Adr3__0 = immed ? 5'b00010 : 5'bz;  // Controlled_Buffer controlled_buffer_1
  assign Adr3__0 = memdir ? 5'b00011 : 5'bz;  // Controlled_Buffer controlled_buffer_2
  assign Adr3__0 = regdir ? 5'b00100 : 5'bz;  // Controlled_Buffer controlled_buffer_3
  assign Adr3__0 = memind ? 5'b00110 : 5'bz;  // Controlled_Buffer controlled_buffer_4
  assign Adr3__0 = postincr ? 5'b01100 : 5'bz;  // Controlled_Buffer controlled_buffer_5
  assign Adr3__0 = pcrelpom ? 5'b10000 : 5'bz;  // Controlled_Buffer controlled_buffer_6
endmodule
