// Logisim project ORT2Project.circ as structural Verilog: 8 circuits, main circuit COMPUTER
module COMPUTER (
);

  wire BTN_RST_out, CLK, cpu_1_inta, interrupt_interface_4_1_p4, interrupt_interface_4_1_p5,
       interrupt_interface_4_1_p6, interrupt_interface_4_1_p7, pull_resistor_2_node, pull_resistor_6_node,
       ram_1_out_8, rst;
  wire [1:0] cpu_1_uext1__0;
  wire [3:0] interrupt_interface_4_1_p1;
  wire [7:0] pull_resistor_1_node, ram_1_out_7;
  wire [15:0] pull_resistor_4_node;

  Button BTN_RST (.out(BTN_RST_out));
  Clock u_CLK (.out(CLK));
  // RisingEdge risingedge_1: pin names not known; wires that end beside it: BTN_RST_out, CLK, rst
  RAM ram_1 (
    .in_1(pull_resistor_4_node), .in_2(CLK), .in_3(pull_resistor_1_node), .in_4(pull_resistor_2_node),
    .in_5(pull_resistor_6_node), .in_6(rst), .out_7(ram_1_out_7), .out_8(ram_1_out_8));
  Pull_Resistor pull_resistor_1 (.node(pull_resistor_1_node));
  Pull_Resistor pull_resistor_2 (.node(pull_resistor_2_node));
  Pull_Resistor pull_resistor_3 (.node(ram_1_out_7));
  Pull_Resistor pull_resistor_4 (.node(pull_resistor_4_node));
  Pull_Resistor pull_resistor_5 (.node(ram_1_out_8));
  Pull_Resistor pull_resistor_6 (.node(pull_resistor_6_node));
  CPU cpu_1 (
    .in_1(rst), .in_2(CLK), .in_3(ram_1_out_8), .in_4(ram_1_out_7), .ABUS(pull_resistor_4_node),
    .DOUTBUS(pull_resistor_1_node), .out_8(pull_resistor_2_node), .out_9(pull_resistor_6_node),
    .inta(cpu_1_inta), .intr3__0(interrupt_interface_4_1_p1), .UEXT1__0(cpu_1_uext1__0));
  // INTERRUPT_INTERFACE_4 interrupt_interface_4_1: pin names not known; wires that end beside it: interrupt_interface_4_1_p1, cpu_1_inta, cpu_1_uext1__0, interrupt_interface_4_1_p4, interrupt_interface_4_1_p5, interrupt_interface_4_1_p6, interrupt_interface_4_1_p7, CLK
  Button BTN_INTR3 (.out(interrupt_interface_4_1_p4));
  Button BTN_INTR2 (.out(interrupt_interface_4_1_p5));
  Button BTN_INTR1 (.out(interrupt_interface_4_1_p6));
  Button BTN_INTR0 (.out(interrupt_interface_4_1_p7));
endmodule

module CPU (
  input  in_1,
  input  in_2,
  input  in_3,
  input  [7:0] in_4,
  input  [3:0] intr3__0,
  output [15:0] ABUS,
  output [7:0] DOUTBUS,
  output out_8,
  output out_9,
  output inta,
  output [1:0] UEXT1__0
);

  wire [3:0] common_1_phaseffbus;
  wire [5:0] common_1_addrbus, pull_resistor_2_node;
  wire [7:0] A, ALU, PSW, pull_resistor_4_node;
  wire [8:0] pull_resistor_5_node;
  wire [14:0] pull_resistor_6_node;
  wire [15:0] B, INTRADDR;
  wire [19:0] common_1_instrucbus;

  COMMON common_1 (
    .CLK(in_2), .RST(in_1), .DIN(in_4), .CMEMBUS(pull_resistor_6_node), .MAR(ABUS), .MDR(DOUTBUS),
    .PHASEFFBUS(common_1_phaseffbus), .ADDRBUS(common_1_addrbus), .PSW(PSW), .CREGBUS(pull_resistor_5_node),
    .CFFBUS(pull_resistor_4_node), .B(B), .A(A), .CPSW(pull_resistor_2_node), .ALU(ALU), .IVTPPDSP(INTRADDR),
    .INSTRUCBUS(common_1_instrucbus));
  Pull_Resistor pull_resistor_1 (.node(common_1_phaseffbus));
  Pull_Resistor pull_resistor_2 (.node(pull_resistor_2_node));
  Pull_Resistor pull_resistor_3 (.node(common_1_instrucbus));
  Pull_Resistor pull_resistor_4 (.node(pull_resistor_4_node));
  Pull_Resistor pull_resistor_5 (.node(pull_resistor_5_node));
  Pull_Resistor pull_resistor_6 (.node(pull_resistor_6_node));
  Pull_Resistor pull_resistor_7 (.node(common_1_addrbus));
  FETCH fetch_1 (
    .in_1(in_1), .in_2(in_2), .in_3(in_3), .PHASEFFBUS(common_1_phaseffbus), .in_5(common_1_instrucbus),
    .in_6(common_1_addrbus), .PSW(PSW), .rdMEM(out_9), .CMEMBUS(pull_resistor_6_node),
    .CFFBUS(pull_resistor_4_node), .CREGBUS(pull_resistor_5_node));
  ADDR addr_1 (
    .in_1(in_1), .in_2(in_2), .in_3(in_3), .PHASEFFBUS(common_1_phaseffbus),
    .INSTRUCBUS(common_1_instrucbus), .ADDRBUS(common_1_addrbus), .rdMEM(out_9),
    .CMEMBUS(pull_resistor_6_node), .CFFBUS(pull_resistor_4_node), .CREGBUS(pull_resistor_5_node));
  EXEC exec_1 (
    .in_1(in_1), .in_2(in_2), .in_3(in_3), .B(B), .PHASEFFBUS(common_1_phaseffbus),
    .INSTRUCBUS(common_1_instrucbus), .ADDRBUS(common_1_addrbus), .PSW(PSW), .A(A), .ALU(ALU),
    .CMEMBUS(pull_resistor_6_node), .CFFBUS(pull_resistor_4_node), .CREGBUS(pull_resistor_5_node),
    .CPSW(pull_resistor_2_node), .rdMEM(out_9), .wrMEM(out_8));
  INTR intr_1 (
    .in_1(in_1), .in_2(in_2), .in_3(in_3), .PHASEFFBUS(common_1_phaseffbus),
    .INSTRUCBUS(common_1_instrucbus), .PSW(PSW), .intr(intr3__0), .ADDIVTP(INTRADDR),
    .CMEMBUS(pull_resistor_6_node), .CFFBUS(pull_resistor_4_node), .CREGBUS(pull_resistor_5_node),
    .rdMEM(out_9), .wrMEM(out_8), .UEXT1__0(UEXT1__0), .inta(inta));
  // Pins of 8 and 16 bits meet at B

  // Other names for the same wires on the sheet: CLK = in_2; DIN7__0[7:0] = in_4; FCBUS = in_3; MAR[15:0] = ABUS;
  //   MDR[7:0] = DOUTBUS; RD = out_9; rst = in_1; WR = out_8
endmodule

module COMMON (
  input  CLK,
  input  RST,
  input  [7:0] DIN,
  input  [7:0] A,
  input  [7:0] ALU,
  input  [15:0] IVTPPDSP,
  input  [14:0] CMEMBUS,
  input  [7:0] CFFBUS,
  input  [8:0] CREGBUS,
  input  [5:0] CPSW,
  output [15:0] MAR,
  output [7:0] MDR,
  output [3:0] PHASEFFBUS,
  output [19:0] INSTRUCBUS,
  output [5:0] ADDRBUS,
  output [7:0] PSW,
  output [15:0] B
);

  wire adrinstr, bezadrinstr, brnchinstr, jmpinstr, mp4_16b_1_p5, mp4_16b_2_p5, mxB0, mxB1, not_1_out,
       not_4_out, reg16_inc_ld_2_p4, reg16_inc_ld_2_p5, rsff_2_p4, rsff_3_p4, rsff_5_p4;
  wire [3:0] IR27__24, mp4_4b_1_p5;
  wire [7:0] DWH, DWL, IR7__0, IR15__8, IR23__16;
  wire [7:4] IR31__24;
  wire [15:0] ADDPCREL15__0, mp8_16b_1_p6, outGPR, PC15__0;

  // MP4_16b mp4_16b_1: pin names not known; wires that end beside it: CMEMBUS[11], CMEMBUS[10], outGPR, ADDPCREL15__0, mp4_16b_1_p5, {IR7__0, IR15__8}, {DWH, DWL}, 1'b1
  // REG16_INC_LD reg16_inc_ld_1: pin names not known; wires that end beside it: CLK, mp4_16b_1_p5, MAR, CMEMBUS[0], CMEMBUS[1]
  // REG8_LD reg8_ld_1: pin names not known; wires that end beside it: CLK, MDR, IR23__16, CREGBUS[6]
  // DC4_16 dc4_16_1: pin names not known; wires that end beside it: IR27__24, bezadrinstr, INSTRUCBUS[0], INSTRUCBUS[1], INSTRUCBUS[2], INSTRUCBUS[3], INSTRUCBUS[4], INSTRUCBUS[5], INSTRUCBUS[6]
  // DC4_16 dc4_16_2: pin names not known; wires that end beside it: IR27__24, brnchinstr, INSTRUCBUS[7], INSTRUCBUS[8], INSTRUCBUS[9], INSTRUCBUS[10], INSTRUCBUS[11], INSTRUCBUS[12]
  // ADD16 add16_1: pin names not known; wires that end beside it: {{9{IR15__8[7]}}, IR15__8[6:0]}, ADDPCREL15__0, PC15__0
  // REG8_LD reg8_ld_2: pin names not known; wires that end beside it: CLK, MDR, {IR31__24, IR27__24}, CREGBUS[7]
  // DC4_16 dc4_16_3: pin names not known; wires that end beside it: IR31__24, PSW[0], bezadrinstr, brnchinstr, jmpinstr, adrinstr
  // MP4_16b mp4_16b_2: pin names not known; wires that end beside it: mxB1, mxB0, {IR7__0, IR15__8}, outGPR, mp4_16b_2_p5, {MDR, DWL}, 1'b1
  // REG16 reg16_1: pin names not known; wires that end beside it: CLK, mp4_16b_2_p5, B, CREGBUS[3]
  // REG8_LD reg8_ld_3: pin names not known; wires that end beside it: CLK, DIN, MDR, CMEMBUS[2]
  // REG8_LD reg8_ld_4: pin names not known; wires that end beside it: CLK, MDR, IR7__0, CREGBUS[4]
  // REG8_LD reg8_ld_5: pin names not known; wires that end beside it: CLK, MDR, IR15__8, CREGBUS[5]
  // DC4_16 dc4_16_4: pin names not known; wires that end beside it: IR27__24, jmpinstr, INSTRUCBUS[13], INSTRUCBUS[14]
  // DC4_16 dc4_16_5: pin names not known; wires that end beside it: IR27__24, adrinstr, INSTRUCBUS[15], INSTRUCBUS[16], INSTRUCBUS[17], INSTRUCBUS[18], INSTRUCBUS[19]
  // DC3_8 dc3_8_1: pin names not known; wires that end beside it: IR23__16[7:5], adrinstr, ADDRBUS[0], ADDRBUS[1], ADDRBUS[2], ADDRBUS[3], ADDRBUS[4], ADDRBUS[5]
  // REG8_LD reg8_ld_6: pin names not known; wires that end beside it: CLK, MDR, DWH, CREGBUS[2]
  not not_1 (not_1_out, RST);
  // RSFF rsff_1: pin names not known; wires that end beside it: CFFBUS[1], CLK, CFFBUS[0], not_1_out, PHASEFFBUS[0]
  // REG16_INC_LD reg16_inc_ld_2: pin names not known; wires that end beside it: CLK, 16'h1000, PC15__0, reg16_inc_ld_2_p4, reg16_inc_ld_2_p5, reg16_inc_ld_2_p5
  or or_1 (reg16_inc_ld_2_p4, CMEMBUS[3], RST);
  // REG8_LD reg8_ld_7: pin names not known; wires that end beside it: CLK, MDR, DWL, CREGBUS[1]
  // RSFF rsff_2: pin names not known; wires that end beside it: CFFBUS[3], CLK, CFFBUS[2], rsff_2_p4, PHASEFFBUS[1]
  not not_2 (rsff_2_p4, RST);
  // RSFF rsff_3: pin names not known; wires that end beside it: CFFBUS[5], CLK, CFFBUS[4], rsff_3_p4, PHASEFFBUS[2]
  not not_3 (rsff_3_p4, RST);
  // MP4_4b mp4_4b_1: pin names not known; wires that end beside it: CMEMBUS[6], CMEMBUS[5], 4'b0010, 4'b0001, mp4_4b_1_p5, 4'b0000, IR23__16[3:0], 1'b1
  GPR16x16 gpr16x16_1 (
    .DI15__0(mp8_16b_1_p6), .A3__0(mp4_4b_1_p5), .WR(CREGBUS[0]), .CLK(CLK),
    .REGSIG7__0({{6{1'b0}}, CMEMBUS[4], RST}), .DO15__0(outGPR));
  not not_4 (not_4_out, RST);
  // RSFF rsff_4: pin names not known; wires that end beside it: CPSW[0], CLK, not_4_out, PSW[0]
  // MP8_16b mp8_16b_1: pin names not known; wires that end beside it: CMEMBUS[9], CMEMBUS[8], CMEMBUS[7], {16{1'b0}}, B, mp8_16b_1_p6, 1'b1
  // RSFF rsff_5: pin names not known; wires that end beside it: CFFBUS[7], CLK, CFFBUS[6], rsff_5_p4, PHASEFFBUS[3]
  not not_5 (rsff_5_p4, RST);

  // Other names for the same wires on the sheet: MDR7__0[7:0] = MDR; incPC = CMEMBUS[4]; A7__0[7:0] = A;
  //   immed = ADDRBUS[0]; memdir = ADDRBUS[1]; regdir = ADDRBUS[2]; memind = ADDRBUS[3]; postincr = ADDRBUS[4];
  //   pcrelpom = ADDRBUS[5]; ALU7__0[7:0] = ALU; B15__0[15:0] = B; stFETCH = CFFBUS[0]; clFETCH = CFFBUS[1];
  //   stADDR = CFFBUS[2]; clADDR = CFFBUS[3]; stEXEC = CFFBUS[4]; clEXEC = CFFBUS[5]; stINTR = CFFBUS[6];
  //   clINTR = CFFBUS[7]; ldMAR = CMEMBUS[0]; incMAR = CMEMBUS[1]; ldMDR = CMEMBUS[2]; ldPC = CMEMBUS[3];
  //   mxaGPR0 = CMEMBUS[5]; mxaGPR1 = CMEMBUS[6]; mxGPR0 = CMEMBUS[7]; mxGPR1 = CMEMBUS[8]; mxGPR2 = CMEMBUS[9];
  //   mxMAR0 = CMEMBUS[10]; mxMAR1 = CMEMBUS[11]; clPSWSTART = CPSW[0]; wrGPR = CREGBUS[0]; ldDWL = CREGBUS[1];
  //   ldDWH = CREGBUS[2]; ldB = CREGBUS[3]; ldIR7__0 = CREGBUS[4]; ldIR15__8 = CREGBUS[5]; ldIR23__16 = CREGBUS[6];
  //   ldIR31__24 = CREGBUS[7]; Din7__0[7:0] = DIN; ENTRADDR15__0[15:0] = IVTPPDSP; HALT = INSTRUCBUS[0];
  //   RTS = INSTRUCBUS[1]; RTI = INSTRUCBUS[2]; ASL = INSTRUCBUS[3]; ROLC = INSTRUCBUS[4]; PUSHGPR = INSTRUCBUS[5];
  //   POPGPR = INSTRUCBUS[6]; BLSS = INSTRUCBUS[7]; BNCR = INSTRUCBUS[8]; BGRTU = INSTRUCBUS[9];
  //   BNEG = INSTRUCBUS[10]; JLEQ = INSTRUCBUS[11]; LOOPGRE = INSTRUCBUS[12]; JMP = INSTRUCBUS[13];
  //   JSR = INSTRUCBUS[14]; LD = INSTRUCBUS[15]; ST = INSTRUCBUS[16]; SUB = INSTRUCBUS[17]; AND = INSTRUCBUS[18];
  //   NOT = INSTRUCBUS[19]; IR31__24[3:0] = IR27__24; MAR15__0[15:0] = MAR; FETCH = PHASEFFBUS[0];
  //   ADDR = PHASEFFBUS[1]; EXEC = PHASEFFBUS[2]; INTR = PHASEFFBUS[3]; PSWSTART = PSW[0]

  // Notes on the sheet:
  //   Sabirac
  //   Instrukcijski registar
  //   Pomocni registri
  //   MAR
  //   Dekoderi za prepoznavanje instrukcije na osnovu sadrzaja registra IR23..16
  //   MDR
  //   PC
  //   FF za pokretanje FETCH, ADDR, EXEC i INTR faze izvršavanja instrukcije
  //   Registri opste namen(PC, SP, ACC + ostali)
  //   Programska statusna reč (PSW)
endmodule

// brI2_arlog
module FETCH (
  input  in_1,
  input  in_2,
  input  in_3,
  input  [3:0] PHASEFFBUS,
  input  [19:0] in_5,
  input  [5:0] in_6,
  input  [7:0] PSW,
  output [14:0] CMEMBUS,
  output [7:0] CFFBUS,
  output [8:0] CREGBUS,
  output rdMEM
);

  wire and_3_out, and_4_out, and_5_out, and_6_out, and_7_out, and_8_out, and_9_out, and_10_out, and_11_out,
       and_12_out, and_13_out, brcnd, brgradr, brgrinst, brI1bezadr, brI2arlog, brI2brnch, brI3arlog,
       brI3brnch_jmp, brnotfcbus, bruncnd, clFETCH, gradr, grinst, I1_bezadr, I2_arlog, I2_brnch, I3_arlog,
       I3_brnch, I3_brnch_jmp, I3_jmp, incPC, ldIR7__0, ldIR15__8, ldIR23__16, ldIR31__24, ldMAR, ldMDR,
       not_1_out, not_3_out, not_5_out, notPSWSTandFETCH, or_6_out, or_7_out, or_9_out, or_10_out, or_11_out,
       or_12_out, or_13_out, rdMEM_t, reg5_cl_inc_ld_1_p5, reg5_cl_inc_ld_1_p6, stADDR, stEXEC;
  wire [4:0] reg5_cl_inc_ld_1_p4;
  wire [23:11] rom32x24_1_dout;

  or or_1 (I2_brnch, in_5[7], in_5[8], in_5[9], in_5[10]);
  or or_2 (I1_bezadr, in_5[0], in_5[1], in_5[2], in_5[3], in_5[4], in_5[5], in_5[6]);
  not not_1 (not_1_out, in_1);
  // REG5_CL_INC_LD reg5_cl_inc_ld_1: pin names not known; wires that end beside it: in_2, not_1_out, rom32x24_1_dout[20:16], reg5_cl_inc_ld_1_p4, reg5_cl_inc_ld_1_p5, reg5_cl_inc_ld_1_p6
  ROM32x24 rom32x24_1 (
    .A4__0(reg5_cl_inc_ld_1_p4), .CS(1'b1),
    .DOUT({rom32x24_1_dout, stEXEC, stADDR, clFETCH, ldIR7__0, ldIR15__8, ldIR23__16, ldIR31__24, ldMDR, rdMEM_t, incPC, ldMAR}));
  not not_2 (reg5_cl_inc_ld_1_p6, reg5_cl_inc_ld_1_p5);
  or or_3 (I3_brnch, in_5[11], in_5[12]);
  or or_4 (I3_jmp, in_5[13], in_5[14]);
  or or_5 (reg5_cl_inc_ld_1_p5, bruncnd, brcnd);
  or or_6 (or_6_out, in_5[15], in_5[16], in_5[17], in_5[18], in_5[19]);
  or or_7 (or_7_out, in_6[2], in_6[4]);
  and and_1 (I2_arlog, or_6_out, or_7_out);
  or or_8 (I3_brnch_jmp, I3_brnch, I3_jmp);
  or or_9 (or_9_out, in_5[15], in_5[16], in_5[17], in_5[18], in_5[19]);
  and and_2 (I3_arlog, or_9_out, in_6[5]);
  // DC4_16 dc4_16_1: pin names not known; wires that end beside it: rom32x24_1_dout[15:12], 1'b1, bruncnd, notPSWSTandFETCH, brI1bezadr, brI2brnch, brI2arlog, brI3brnch_jmp, brI3arlog, brnotfcbus, brgrinst, brgradr
  or or_10 (or_10_out, in_5[15], in_5[16], in_5[17], in_5[18], in_5[19]);
  or or_11 (or_11_out, in_6[0], in_6[1], in_6[2], in_6[3], in_6[4], in_6[5]);
  not not_3 (not_3_out, or_11_out);
  not not_4 (grinst, or_12_out);
  and and_3 (and_3_out, or_10_out, not_3_out);
  and and_4 (and_4_out, in_5[16], in_6[0]);
  or or_12 (or_12_out, in_5[0], in_5[1], in_5[2], in_5[3], in_5[4], in_5[5], in_5[6], in_5[7], in_5[8], in_5[9], in_5[10], in_5[11], in_5[12], in_5[13], in_5[14], in_5[15], in_5[16], in_5[17], in_5[18], in_5[19]);
  or or_13 (or_13_out, ~PHASEFFBUS[0], ~PSW[0]);  // OR_Gate
  not not_5 (not_5_out, in_3);
  or or_14 (gradr, and_3_out, and_4_out);
  and and_5 (and_5_out, or_13_out, notPSWSTandFETCH);
  and and_6 (and_6_out, I1_bezadr, brI1bezadr);
  and and_7 (and_7_out, I2_brnch, brI2brnch);
  and and_8 (and_8_out, I2_arlog, brI2arlog);
  and and_9 (and_9_out, I3_brnch_jmp, brI3brnch_jmp);
  and and_10 (and_10_out, I3_arlog, brI3arlog);
  and and_11 (and_11_out, brnotfcbus, not_5_out);
  and and_12 (and_12_out, grinst, brgrinst);
  and and_13 (and_13_out, gradr, brgradr);
  or or_15 (brcnd, and_5_out, and_6_out, and_7_out, and_8_out, and_9_out, and_10_out, and_11_out, and_12_out, and_13_out);
  assign CMEMBUS[0] = ldMAR ? 1'b1 : 1'bz;  // Controlled_Buffer controlled_buffer_1
  assign CMEMBUS[2] = ldMDR ? 1'b1 : 1'bz;  // Controlled_Buffer controlled_buffer_2
  assign CMEMBUS[4] = incPC ? 1'b1 : 1'bz;  // Controlled_Buffer controlled_buffer_3
  assign CREGBUS[4] = ldIR7__0 ? 1'b1 : 1'bz;  // Controlled_Buffer controlled_buffer_4
  assign CREGBUS[5] = ldIR15__8 ? 1'b1 : 1'bz;  // Controlled_Buffer controlled_buffer_5
  assign CREGBUS[6] = ldIR23__16 ? 1'b1 : 1'bz;  // Controlled_Buffer controlled_buffer_6
  assign CREGBUS[7] = ldIR31__24 ? 1'b1 : 1'bz;  // Controlled_Buffer controlled_buffer_7
  assign CFFBUS[1] = clFETCH ? 1'b1 : 1'bz;  // Controlled_Buffer controlled_buffer_8
  assign CFFBUS[2] = stADDR ? 1'b1 : 1'bz;  // Controlled_Buffer controlled_buffer_9
  assign CFFBUS[4] = stEXEC ? 1'b1 : 1'bz;  // Controlled_Buffer controlled_buffer_10
  assign rdMEM = rdMEM_t ? 1'b1 : 1'bz;  // Controlled_Buffer controlled_buffer_11

  // Other names for the same wires on the sheet: CLK = in_2; FCBUS = in_3; HALT = in_5[0]; RTS = in_5[1];
  //   RTI = in_5[2]; ASL = in_5[3]; ROLC = in_5[4]; PUSHGPR = in_5[5]; POPGPR = in_5[6]; BLSS = in_5[7];
  //   BNCR = in_5[8]; BGRTU = in_5[9]; BNEG = in_5[10]; JLEQ = in_5[11]; LOOPGRE = in_5[12]; JMP = in_5[13];
  //   JSR = in_5[14]; LD = in_5[15]; ST = in_5[16]; SUB = in_5[17]; AND = in_5[18]; NOT = in_5[19]; immed = in_6[0];
  //   memdir = in_6[1]; regdir = in_6[2]; memind = in_6[3]; postincr = in_6[4]; pcrelpom = in_6[5];
  //   FETCH = PHASEFFBUS[0]; ADDR = PHASEFFBUS[1]; EXEC = PHASEFFBUS[2]; INTR = PHASEFFBUS[3]; PSWSTART = PSW[0];
  //   rst = in_1

  // Notes on the sheet:
  //   Operaciona jedinica
  //   Kontrolna jedinica
  //   ako je adresna funkcija a nijedan nacin adresiranja nije ukljucen ili ST + immed
endmodule

module ADDR (
  input  in_1,
  input  in_2,
  input  in_3,
  input  [3:0] PHASEFFBUS,
  input  [19:0] INSTRUCBUS,
  input  [5:0] ADDRBUS,
  output [14:0] CMEMBUS,
  output [7:0] CFFBUS,
  output [8:0] CREGBUS,
  output rdMEM
);

  wire and_1_out, and_2_out, and_3_out, bradr, brcnd, brnotADDR, brnotFCBUS, brSTORE, bruncnd, not_1_out,
       not_3_out, not_4_out, reg5_cl_inc_ld_1_p5, reg5_cl_inc_ld_1_p6;
  wire [2:0] mp2_8b_1_p3, rom32x32_1_dout_3;
  wire [4:0] mp2_8b_1_p4, reg5_cl_inc_ld_1_p3, reg5_cl_inc_ld_1_p4, rom32x32_1_dout_2;
  wire [31:0] rom32x32_1_dout;

  not not_1 (not_1_out, in_1);
  // REG5_CL_INC_LD reg5_cl_inc_ld_1: pin names not known; wires that end beside it: in_2, not_1_out, reg5_cl_inc_ld_1_p3, reg5_cl_inc_ld_1_p4, reg5_cl_inc_ld_1_p5, reg5_cl_inc_ld_1_p6
  ROM32x32 rom32x32_1 (
    .A4__0(reg5_cl_inc_ld_1_p4), .CS(1'b1),
    .DOUT({rom32x32_1_dout[31:29], rom32x32_1_dout_2, rom32x32_1_dout[23], rom32x32_1_dout_3, rom32x32_1_dout[19:0]}));
  not not_2 (reg5_cl_inc_ld_1_p6, reg5_cl_inc_ld_1_p5);
  // MP2_8b mp2_8b_1: pin names not known; wires that end beside it: bradr, {3'b000, rom32x32_1_dout_2}, {mp2_8b_1_p3, reg5_cl_inc_ld_1_p3}, {3'b000, mp2_8b_1_p4}, 1'b1
  or or_1 (reg5_cl_inc_ld_1_p5, bruncnd, brcnd, bradr);
  KMADR6 kmadr6_1 (
    .immed(ADDRBUS[0]), .memdir(ADDRBUS[1]), .regdir(ADDRBUS[2]), .memind(ADDRBUS[3]), .postincr(ADDRBUS[4]),
    .pcrelpom(ADDRBUS[5]), .Adr3__0(mp2_8b_1_p4));
  // DC3_8 dc3_8_1: pin names not known; wires that end beside it: rom32x32_1_dout_3, 1'b1, bruncnd, brnotADDR, brSTORE, brnotFCBUS, bradr
  not not_3 (not_3_out, PHASEFFBUS[1]);
  not not_4 (not_4_out, in_3);
  and and_1 (and_1_out, not_3_out, brnotADDR);
  and and_2 (and_2_out, INSTRUCBUS[16], brSTORE);
  and and_3 (and_3_out, brnotFCBUS, not_4_out);
  or or_2 (brcnd, and_1_out, and_2_out, and_3_out);

  // Other names for the same wires on the sheet: immed = ADDRBUS[0]; memdir = ADDRBUS[1]; regdir = ADDRBUS[2];
  //   memind = ADDRBUS[3]; postincr = ADDRBUS[4]; pcrelpom = ADDRBUS[5]; CLK = in_2; FCBUS = in_3;
  //   ST = INSTRUCBUS[16]; ADDR = PHASEFFBUS[1]; rst = in_1

  // Notes on the sheet:
  //   Operaciona jedinica
  //   Upravljacka jedinica
endmodule

module EXEC (
  input  in_1,
  input  in_2,
  input  in_3,
  input  [15:0] B,
  input  [3:0] PHASEFFBUS,
  input  [19:0] INSTRUCBUS,
  input  [5:0] ADDRBUS,
  input  [7:0] PSW,
  output [7:0] A,
  output [7:0] ALU,
  output [14:0] CMEMBUS,
  output [7:0] CFFBUS,
  output [8:0] CREGBUS,
  output [5:0] CPSW,
  output rdMEM,
  output wrMEM
);


  // Other names for the same wires on the sheet: A7__0[7:0] = A; ALU7__0[7:0] = ALU; B15__0[15:0] = B; CLK = in_2;
  //   FCBUS = in_3; rst = in_1

  // Notes on the sheet:
  //   Operaciona jedinica
  //   Upravljacka jedinica
endmodule

module INTR (
  input  in_1,
  input  in_2,
  input  in_3,
  input  [3:0] PHASEFFBUS,
  input  [19:0] INSTRUCBUS,
  input  [7:0] PSW,
  input  [3:0] intr,
  output [15:0] ADDIVTP,
  output [1:0] UEXT1__0,
  output inta,
  output [14:0] CMEMBUS,
  output [7:0] CFFBUS,
  output [8:0] CREGBUS,
  output rdMEM,
  output wrMEM
);


  // Other names for the same wires on the sheet: ADDIVTP15__0[15:0] = ADDIVTP; CLK = in_2; FCBUS = in_3;
  //   intr3__0[3:0] = intr; ldBR = inta; rst = in_1

  // Notes on the sheet:
  //   Operaciona jedinica
  //   Upravljacka jedinica
endmodule

module RAM (
  input  [15:0] in_1,
  input  in_2,
  input  [7:0] in_3,
  input  in_4,
  input  in_5,
  input  in_6,
  output [7:0] out_7,
  output out_8
);

  wire and_1_out, and_2_out, CNT0, LDCNT, not_1_out, notCNT0, or_1_out, reg4_ld_sl_sr_1_p6, rsff_2_p4,
       rsff_2_p5, rsff_3_p4, sl;
  wire [3:0] CNT, LFSR;

  // RSFF rsff_1: pin names not known; wires that end beside it: 1'b0, in_2, in_6, sl
  or or_1 (or_1_out, in_4, in_5);
  // REG4_LD_SL_SR reg4_ld_sl_sr_1: pin names not known; wires that end beside it: 1'b0, 1'b0, in_2, 4'b1111, LFSR, reg4_ld_sl_sr_1_p6, sl, in_6
  // RisingEdge risingedge_1: pin names not known; wires that end beside it: or_1_out, in_2, LDCNT
  // MEM64Kx8 mem64kx8_1: pin names not known; wires that end beside it: in_1, 1'b1, in_2, in_3, out_7, in_4
  xor xor_1 (reg4_ld_sl_sr_1_p6, LFSR[2], LFSR[3]);
  and and_1 (and_1_out, CNT0, not_1_out);
  not not_1 (not_1_out, LDCNT);
  // RSFF rsff_2: pin names not known; wires that end beside it: and_1_out, in_2, LDCNT, rsff_2_p4, rsff_2_p5
  not not_2 (rsff_2_p4, in_6);
  and and_2 (and_2_out, rsff_2_p5, CNT0);
  // REG4m_DEC_LD reg4m_dec_ld_1: pin names not known; wires that end beside it: in_2, LFSR, CNT, LDCNT, notCNT0, notCNT0
  or or_2 (notCNT0, CNT[0], CNT[1], CNT[2], CNT[3]);
  // RSFF rsff_3: pin names not known; wires that end beside it: out_8, in_2, and_2_out, rsff_3_p4, out_8
  not not_3 (rsff_3_p4, in_6);
  not not_4 (CNT0, notCNT0);

  // Other names for the same wires on the sheet: ADR[15:0] = in_1; CLK = in_2; DIN[7:0] = in_3; DOUT[7:0] = out_7;
  //   fc = out_8; RDMEM = in_5; rst = in_6; WRMEM = in_4

  // Notes on the sheet:
  //   Random broj predstavlja vreme pristupa memoriji
  //   Brojac za generisanje random broja 
  //   Jedinica za generisanje function complete (fc) signala
  //   Brojac za dekrementiranje random broja
endmodule
